// Digital circuit 8 bit procssor.dig as structural Verilog
module _8_bit_procssor (
  input  [7:0] InstrMem_input,
  input  [1:0] InstrMem_ctrl,
  input  clk,
  output [2:0] Program_Counter,
  output [7:0] IR_output,
  output [1:0] IR_ctrl,
  output Inst_Fetch,
  output Inst_Decode,
  output Inst_Exec,
  output Write_Back,
  output [7:0] RegFile_ctrl,
  output [7:0] ALU_output
);

  wire and_1_out, not_1_out, not_2_out;
  wire [7:0] multiplexer_1_out, multiplexer_3_out, register_file_4x8_2r1w_1_rd1,
       register_file_4x8_2r1w_1_rd2, sram_1_data;
  wire [7:3] pc8_1_pc;

  PC8 pc8_1 (
    .INC(Write_Back), .LD(1'b0), .Val({8{1'b0}}), .RST(InstrMem_ctrl[1]), .CLK(clk),
    .PC({pc8_1_pc, Program_Counter}));
  not not_1 (not_1_out, InstrMem_ctrl[1]);
  and and_1 (and_1_out, InstrMem_ctrl[0], not_1_out);
  SRAM sram_1 (
    .ADDR({1'b0, Program_Counter}), .DATA_IN(InstrMem_input), .STORE(and_1_out), .CLK(clk), .SET(1'b1),
    .DATA(sram_1_data));
  not not_2 (not_2_out, and_1_out);
  and and_2 (IR_ctrl[0], Inst_Fetch, not_2_out);
  Control_Unit control_unit_1 (
    .clk(clk), .Write_Back(Write_Back), .Inst_Exec(Inst_Exec), .Inst_Decode(Inst_Decode),
    .Inst_Fetch(Inst_Fetch));
  IR8 ir8_1 (.D_IN_0(sram_1_data), .CLK(clk), .LD(IR_ctrl[0]), .IR(IR_output));
  Multiplexer #(.Selector_Bits(2), .Bits(8)) multiplexer_1 (
    .sel(IR_output[4:3]), .in_0(8'h1), .in_1(8'h4), .in_2(8'h10), .in_3(8'h40), .out(multiplexer_1_out));
  Multiplexer #(.Bits(8)) multiplexer_2 (
    .sel(Write_Back), .in_0({8{1'b0}}), .in_1(multiplexer_1_out), .out(RegFile_ctrl));
  REGISTER_FILE_4x8_2R1W register_file_4x8_2r1w_1 (
    .RR1(IR_output[4:3]), .RR2(IR_output[2:1]), .WR(IR_output[4:3]),
    .CTRL({RegFile_ctrl[6], RegFile_ctrl[4], RegFile_ctrl[2], RegFile_ctrl[0]}), .clk(clk), .WD(ALU_output),
    .RD1(register_file_4x8_2r1w_1_rd1), .RD2(register_file_4x8_2r1w_1_rd2));  // open: Q1, Q2, Q3, Q4
  Multiplexer #(.Bits(8)) multiplexer_3 (
    .sel(IR_output[0]), .in_0(register_file_4x8_2r1w_1_rd1), .in_1({{6{1'b0}}, IR_output[2:1]}),
    .out(multiplexer_3_out));
  ALU8 alu8_1 (
    .A(multiplexer_3_out), .B(register_file_4x8_2r1w_1_rd2), .C_in(IR_output[5]), .S_0(IR_output[6]),
    .S_1(IR_output[7]), .D(ALU_output));

  assign IR_ctrl[1] = 1'b0;
endmodule

/* Test case:
clk Program_Counter InstrMem_input InstrMem_ctrl IR_output IR_ctrl Write_Back ALU_output

C X 143 1 X X X X
repeat(3) C X 0 0 X X X X

C X 147 1 X X X X
repeat(3) C X 0 0 X X X X

C X 12 1 X X X X
repeat(3) C X 0 0 X X X X

C X 108 1 X X X X
repeat(3) C X 0 0 X X X X

C X 168 1 X X X X
repeat(3) C X 0 0 X X X X

C X 200 1 X X X X
repeat(3) C X 0 0 X X X X

C X 44 1 X X X X
repeat(3) C X 0 0 X X X X

C X 136 1 X X X X
repeat(3) C X 0 0 X X X X

repeat(40) C X 0 0 X X X X
*/
